# Fritzing sketch Tegninger (saved by Fritzing 0.9.9b)
breadboards: 1

parts:
  Part3 = Arduino Motor Shield (Rev3)
  Part4 = Arduino Uno (Rev3)
  M2 = DC Motor
  M1 = DC Motor
  IC1 = IC, DIP package, 16 pins [chip_label=CD4051BE]
  S2 = Round Pushbutton
  S3 = Round Pushbutton
  S4 = Round Pushbutton
  S5 = Round Pushbutton
  S6 = Round Pushbutton
  S1 = Pushbutton [package="[THT]"]
  R1 = Resistor [tolerance=±5% resistance=110 package="0603 [SMD]"]
  R2 = Resistor [tolerance=±5% resistance=110 package="0603 [SMD]"]
  R3 = Resistor [tolerance=±5% resistance=110 package="0603 [SMD]"]
  R4 = Resistor [tolerance=±5% resistance=110 package="0603 [SMD]"]
  R5 = Resistor [tolerance=±5% resistance=110 package="0603 [SMD]"]
  R6 = Resistor [tolerance=±5% resistance=110 package="0603 [SMD]"]
  R7 = Resistor [tolerance=±5% resistance=110 package="0603 [SMD]"]
  LED1 = LEDs [package=led10mm]
  LED2 = LEDs [package=led10mm]
  LED3 = LEDs [package=led10mm]
  LED4 = LEDs [package=led10mm]
  LED5 = LEDs [package=led10mm]
  LED6 = LEDs [package=led10mm]
  LED7 = LEDs [package=led10mm]
  R8 = Resistor [tolerance=±5% resistance=110 package="0603 [SMD]"]
  R9 = Resistor [tolerance=±5% resistance=110 package="0603 [SMD]"]
  R10 = Resistor [tolerance=±5% resistance=2.2k package="0603 [SMD]"]
  R11 = Resistor [tolerance=±5% resistance=2.2k package="0603 [SMD]"]
  Q2 = QRD1114 [package=qrd1114]
  U1 = 74HC595 [package="DIP16 [THT]"]
  VCC1 = Battery
  VCC2 = Battery
  Q1 = QRD1114 [package=qrd1114]

nets (from the schematic view):
  N1: Part3.A5, IC1.pin11
  N2: Part3.D8/BreakeB, IC1.pin3
  N3: Part3.D9/BreakeA, IC1.pin2
  N4: Part3.D10_PWM, IC1.pin1
  N5: Part3.D2, R10.Pin_1, Q2.E
  N6: Part3.D3_PWM/A, Part4.D6_PWM
  N7: Part3.D4, U1.ST_CP
  N8: Part3.D5_PWM, U1.SH_CP
  N9: Part3.D6_PWM, Part4.D3_PWM, R11.Pin_1, Q1.E
  N10: Part3.D7, U1.DS
  N11: Part3.B-, M2.pin_2
  N12: Part3.B+, M2.pin_1
  N13: Part3.A-, M1.pin_2
  N14: Part3.A+, M1.pin_1
  N15: Part3.VMOT, VCC1.+, VCC2.+
  N16: Part3.GND, U1.OE, VCC1.-, VCC2.-
  5V: Part3.5V, IC1.pin8, R8.Pin_0, R9.Pin_0, R10.Pin_0, R11.Pin_0, U1.MR, U1.VCC
  N17: IC1.pin4, S5.leg0
  N18: IC1.pin5, S2.leg0
  N19: IC1.pin6, S3.leg0
  N20: IC1.pin7, S4.leg0
  N21: IC1.pin9, S1.Pin_1, S1.Pin_2
  N22: IC1.pin13, S6.leg0
  GND: IC1.pin14, IC1.pin15, IC1.pin16, S2.leg1, S3.leg1, S4.leg1, S5.leg1, S6.leg1, S1.Pin_3, S1.Pin_4, R1.Pin_1, R2.Pin_1, R3.Pin_1, R4.Pin_1, R5.Pin_1, R6.Pin_1, R7.Pin_1, Q2.C, Q2.K, U1.GND, Q1.C, Q1.K
  N23: R1.Pin_0, LED6.C
  N24: R2.Pin_0, LED4.C
  N25: R3.Pin_0, LED2.C
  N26: R4.Pin_0, LED1.C
  N27: R5.Pin_0, LED3.C
  N28: R6.Pin_0, LED5.C
  N29: R7.Pin_0, LED7.C
  N30: LED1.A, U1.Q7
  N31: LED2.A, U1.Q6
  N32: LED3.A, U1.Q5
  N33: LED4.A, U1.Q4
  N34: LED5.A, U1.Q3
  N35: LED6.A, U1.Q2
  N36: LED7.A, U1.Q1
  N37: R8.Pin_1, Q2.A
  N38: R9.Pin_1, Q1.A

// code stored in the sketch: Untitled.ino

